# Fritzing sketch Circuit_Arduino (saved by Fritzing 0.9.0b)

parts:
  IC1 = MSGEQ7 [package=soic8]
  NEOPIXEL2 = Neopixel Strip -- White (60/m)
  C3 = Electrolytic Capacitor [capacitance=100nF voltage=10V package="100 mil [THT, electrolytic]"]
  R7 = Resistor [tolerance=±5% resistance=200k package="0603 [SMD]"]
  JACK2 = 2.1mm Barrel Jack with Terminal Block
  C4 = Capacitor [package=cap-pth-small2]
  C5 = Electrolytic Capacitor [capacitance=100nF voltage=10V package="100 mil [THT, electrolytic]"]
  C6 = Capacitor [package=cap-pth-small2]
  R8 = Resistor [tolerance=±5% resistance=15k package="0603 [SMD]"]
  R9 = Trimmer Potentiometer [maximum_resistance=10kΩ package=THT]
  R10 = Resistor [tolerance=±5% resistance=220 package="0603 [SMD]"]
  TRRS1 = Stereo Jack (TRS) 3.5mm [package="PG203J [THT]"]
  R11 = Resistor [tolerance=±5% resistance=330 package="0603 [SMD]"]
  Part3 = Arduino Uno (Rev3)

nets:
  N1: IC1.DCOUT, Part3.A0
  N2: IC1.STROBE, Part3.D2
  N3: IC1.AUDIO_IN, C6.1
  N4: IC1.CG, C3.+
  N5: IC1.RESET, Part3.D3_PWM
  N6: IC1.CKIN, C4.2
  N7: NEOPIXEL2.+5V, R11.Pin_0
  N8: NEOPIXEL2.DI, JACK2.POS, C5.+, Part3.5V
  GND: NEOPIXEL2.GND, JACK2.NEG, TRRS1.Sleeve, Part3.GND
  N9: R7.Pin_1, C4.1
  N10: C6.2, R8.Pin_0, R9.leg1
  N11: R8.Pin_1, TRRS1.Tip
  N12: R9.wiper, R10.Pin_0
  N13: R11.Pin_1, Part3.D4

notes:
  To 5V Power
  33pF
  10nF
  100nF
  Audio IN
  To 5V Battery

custom parts:
  Neopixel Strip -- White (60/m): Neopixel Strip, White, 60 pixels per meter.
