# Fritzing sketch Circuit_ESP8266 (saved by Fritzing 0.9.0b)

parts:
  IC1 = MSGEQ7 [package=soic8]
  NEOPIXEL2 = Neopixel Strip -- White (60/m)
  C3 = Electrolytic Capacitor [capacitance=100nF voltage=10V package="100 mil [THT, electrolytic]"]
  R7 = Resistor [tolerance=±5% resistance=200k package="0603 [SMD]"]
  Part2 = FTDI Basic Programmer
  JACK2 = 2.1mm Barrel Jack with Terminal Block
  C4 = Capacitor [package=cap-pth-small2]
  C5 = Electrolytic Capacitor [capacitance=100nF voltage=10V package="100 mil [THT, electrolytic]"]  # not connected
  C6 = Capacitor [package=cap-pth-small2]
  R8 = Resistor [tolerance=±5% resistance=15k package="0603 [SMD]"]
  R9 = Trimmer Potentiometer [maximum_resistance=10kΩ package=THT]
  R10 = Resistor [tolerance=±5% resistance=220 package="0603 [SMD]"]
  R11 = Resistor [tolerance=±5% resistance=330 package="0603 [SMD]"]
  C7 = Electrolytic Capacitor [capacitance=100nF voltage=10V package="100 mil [THT, electrolytic]"]
  U4 = V_REG_LD1117VXX [package=78xxl]
  TRRS1 = Audio Jack (TRS) 3.5mm [package="4Ucon 08780 [THT]"]

nets:
  N1: IC1.AUDIO_IN, C6.1
  N2: IC1.CG, C3.+
  N3: IC1.CKIN, C4.2
  N4: NEOPIXEL2.+5V, R11.Pin_0
  N5: NEOPIXEL2.DI, Part2.POWER, JACK2.POS, C7.+, U4.IN
  GND: NEOPIXEL2.GND, Part2.GND, JACK2.NEG, U4.GND
  N6: R7.Pin_1, C4.1
  N7: C6.2, R8.Pin_0, R9.leg1
  N8: R8.Pin_1, TRRS1.Tip
  N9: R9.wiper, R10.Pin_0

notes:
  To 5V Power
  33pF
  10nF
  100nF
  Audio IN
  To 5V Battery
  UART to computer

custom parts:
  Neopixel Strip -- White (60/m): Neopixel Strip, White, 60 pixels per meter.
