# Fritzing sketch Circuit_ESP8266_Flash (saved by Fritzing 0.9.0b)
breadboards: 1

parts:
  Part3 = FTDI Basic Programmer
  U5 = V_REG_LD1117VXX [package=78xxl]

nets:
  N1: Part3.POWER, U5.IN
  GND: Part3.GND, U5.GND

notes:
  UART to computer
